# Fritzing sketch sketch (saved by Fritzing 0.9.3b)
breadboards: 1

parts:
  Part1 = Arduino Nano (Rev3.0)
  HC-SR04_Sensor_1 = HC-SR04 Ultrasonic Distance Sensor
  Part2 = Bluetooth HC-05 Macho
  R1 = Resistor [tolerance=±5% resistance=10k package="1206 [SMD]"]
  R2 = Resistor [tolerance=±5% resistance=10k package="1206 [SMD]"]
  R3 = Resistor [tolerance=±5% resistance=10k package="1206 [SMD]"]
  NEOPIXEL1 = Neopixel Strip -- White (60/m)

nets:
  N1: Part1.D1/TX, R1.Pin_0
  N2: Part1.D0/RX, Part2.TXD
  N3: Part1.D2, HC-SR04_Sensor_1.ECHO
  N4: Part1.D3, HC-SR04_Sensor_1.TRIG
  N5: Part1.D5, NEOPIXEL1.+5V
  GND: Part1.GND, HC-SR04_Sensor_1.GND, Part2.GND, R3.Pin_0, NEOPIXEL1.GND
  VCC: Part1.5V, HC-SR04_Sensor_1.VCC, Part2.VCC, NEOPIXEL1.DI
  N6: Part2.RXD, R1.Pin_1, R2.Pin_1
  N7: R2.Pin_0, R3.Pin_1

custom parts:
  Neopixel Strip -- White (60/m): Neopixel Strip, White, 60 pixels per meter.
